# Fritzing sketch room-light (saved by Fritzing 1.0.6)
breadboards: 1

parts:
  Part1 = Adafruit Feather HUZZAH ESP8266 [part_number="Adafruit #2821"]
  R1 = PHOTOCELL [package=photocell]
  Adafruit_Infrared_IR_Remote_Transceiver1 = Adafruit Infrared IR Remote Transceiver [mn=Adafruit mpn=#5990 part_number=#5990]
  R2 = Resistor [tolerance=±5% power=0.25W resistance=220 package=THT]
  S1 = Pushbutton [package="[THT]"]

nets:
  N1: Part1.GPIO12/MISO, S1.Pin_3, S1.Pin_4
  N2: Part1.GPIO14/SCK, Adafruit_Infrared_IR_Remote_Transceiver1.IROUT
  N3: Part1.ADC, R1.P$2, R2.Pin_0
  GND: Part1.GND, Adafruit_Infrared_IR_Remote_Transceiver1.GND, R2.Pin_1, S1.Pin_1, S1.Pin_2
  3.3V: Part1.3.3V, R1.P$1, Adafruit_Infrared_IR_Remote_Transceiver1.VIN

custom parts:
  Adafruit Feather HUZZAH ESP8266: his is the Adafruit Feather HUZZAH ESP8266 - our take on an 'all-in-one' ESP8266 WiFi development board with built in USB and battery charging. Its an ESP8266 WiFi module with all the extras you need, ready to rock! We have other boards in the Feather family, check'em out here. At the Feather HUZZAH's heart is an ESP8266 WiFi microcontroller clocked at 80 MHz and at 3.3V logic. This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
